// Digital circuit new8bitadder.dig as structural Verilog
module new8bitadder (
  input  [7:0] A_In,
  input  [7:0] B_In,
  input  Carry_In,
  output [7:0] Sum_Out,
  output Carry_Out
);

  wire add_1_c_o, add_2_c_o, add_3_c_o, add_4_c_o, add_5_c_o, add_6_c_o, add_7_c_o;

  Add add_1 (.a(A_In[7]), .b(B_In[7]), .c_i(Carry_In), .s(Sum_Out[0]), .c_o(add_1_c_o));
  Add add_2 (.a(A_In[6]), .b(B_In[6]), .c_i(add_1_c_o), .s(Sum_Out[1]), .c_o(add_2_c_o));
  Add add_3 (.a(A_In[5]), .b(B_In[5]), .c_i(add_2_c_o), .s(Sum_Out[2]), .c_o(add_3_c_o));
  Add add_4 (.a(A_In[4]), .b(B_In[4]), .c_i(add_3_c_o), .s(Sum_Out[3]), .c_o(add_4_c_o));
  Add add_5 (.a(A_In[3]), .b(B_In[3]), .c_i(add_4_c_o), .s(Sum_Out[4]), .c_o(add_5_c_o));
  Add add_6 (.a(A_In[2]), .b(B_In[2]), .c_i(add_5_c_o), .s(Sum_Out[5]), .c_o(add_6_c_o));
  Add add_7 (.a(A_In[1]), .b(B_In[1]), .c_i(add_6_c_o), .s(Sum_Out[6]), .c_o(add_7_c_o));
  Add add_8 (.a(A_In[0]), .b(B_In[0]), .c_i(add_7_c_o), .s(Sum_Out[7]), .c_o(Carry_Out));
  // Pins of 1 and 8 bits meet at Sum_Out
  // Pins of 1 and 8 bits meet at A_In
  // Pins of 1 and 8 bits meet at B_In
endmodule
